# Fritzing sketch ic74HC595 (saved by Fritzing 0.7.7b)
breadboards: 2

parts:
  U1 = 74HC595 [package="DIP16 [THT]"]  # not connected
  U2 = 74HC595 [package="DIP16 [THT]"]  # not connected
  Pi1 = Adafruit Pi Cobbler  # not connected
  R17 = Resistor [tolerance=±5% resistance=220 package="0603 [SMD]"]
  R18 = Resistor [tolerance=±5% resistance=220 package="0603 [SMD]"]
  R19 = Resistor [tolerance=±5% resistance=220 package="0603 [SMD]"]
  R20 = Resistor [tolerance=±5% resistance=220 package="0603 [SMD]"]
  R21 = Resistor [tolerance=±5% resistance=220 package="0603 [SMD]"]
  R22 = Resistor [tolerance=±5% resistance=220 package="0603 [SMD]"]
  R23 = Resistor [tolerance=±5% resistance=220 package="0603 [SMD]"]
  R24 = Resistor [tolerance=±5% resistance=220 package="0603 [SMD]"]
  R25 = Resistor [tolerance=±5% resistance=220 package="0603 [SMD]"]
  R26 = Resistor [tolerance=±5% resistance=220 package="0603 [SMD]"]
  R27 = Resistor [tolerance=±5% resistance=220 package="0603 [SMD]"]
  R28 = Resistor [tolerance=±5% resistance=220 package="0603 [SMD]"]
  R29 = Resistor [tolerance=±5% resistance=220 package="0603 [SMD]"]
  R30 = Resistor [tolerance=±5% resistance=220 package="0603 [SMD]"]
  R31 = Resistor [tolerance=±5% resistance=220 package="0603 [SMD]"]
  R32 = Resistor [tolerance=±5% resistance=220 package="0603 [SMD]"]
  LED1 = LED - 3mm [color="Red (633nm)" package="3 mm [THT]"]
  LED2 = LED - 3mm [color="Red (633nm)" package="3 mm [THT]"]
  LED3 = LED - 3mm [color="Red (633nm)" package="3 mm [THT]"]
  LED4 = LED - 3mm [color="Red (633nm)" package="3 mm [THT]"]
  LED5 = LED - 3mm [color="Red (633nm)" package="3 mm [THT]"]
  LED6 = LED - 3mm [color="Red (633nm)" package="3 mm [THT]"]
  LED7 = LED - 3mm [color="Red (633nm)" package="3 mm [THT]"]
  LED8 = LED - 3mm [color="Red (633nm)" package="3 mm [THT]"]
  LED9 = LED - 3mm [color="Red (633nm)" package="3 mm [THT]"]
  LED10 = LED - 3mm [color="Red (633nm)" package="3 mm [THT]"]
  LED11 = LED - 3mm [color="Red (633nm)" package="3 mm [THT]"]
  LED12 = LED - 3mm [color="Red (633nm)" package="3 mm [THT]"]
  LED13 = LED - 3mm [color="Red (633nm)" package="3 mm [THT]"]
  LED14 = LED - 3mm [color="Red (633nm)" package="3 mm [THT]"]
  LED15 = LED - 3mm [color="Red (633nm)" package="3 mm [THT]"]
  LED16 = LED - 3mm [color="Red (633nm)" package="3 mm [THT]"]
  VCC2 = Battery block 9V
  C3 = Electrolytic Capacitor [capacitance=100µF voltage=50V package="100 mil [THT, electrolytic]"]
  C4 = Electrolytic Capacitor [capacitance=10µF voltage=50V package="100 mil [THT, electrolytic]"]
  D2 = Rectifier Diode [part_number=1N5400 package="300 mil [THT]"]
  U3 = Voltage Regulator - 3.3V [package="TO220 [THT]"]

nets:
  N1: R17.Pin_0, LED1.cathode
  N2: R17.Pin_1, R18.Pin_1, R19.Pin_1, R20.Pin_1, R21.Pin_1, R22.Pin_1, R23.Pin_1, R24.Pin_1, R25.Pin_1, R26.Pin_1, R27.Pin_1, R28.Pin_1, R29.Pin_1, R30.Pin_1, R31.Pin_1, R32.Pin_1, VCC2.-, C3.+, C4.+
  N3: R18.Pin_0, LED9.cathode
  N4: R19.Pin_0, LED3.cathode
  N5: R20.Pin_0, LED8.cathode
  N6: R21.Pin_0, LED5.cathode
  N7: R22.Pin_0, LED10.cathode
  N8: R23.Pin_0, LED7.cathode
  N9: R24.Pin_0, LED14.cathode
  N10: R25.Pin_0, LED4.cathode
  N11: R26.Pin_0, LED15.cathode
  N12: R27.Pin_0, LED6.cathode
  N13: R28.Pin_0, LED11.cathode
  N14: R29.Pin_0, LED2.cathode
  N15: R30.Pin_0, LED13.cathode
  N16: R31.Pin_0, LED12.cathode
  N17: R32.Pin_0, LED16.cathode
  N18: VCC2.+, C4.-, U3.input_voltage
  N19: C3.-, D2.anode, U3.output_voltage

notes:
  Register 0 is located on the right, with the rightmost top pin cascading to the serial in of the next register.

custom parts:
  Adafruit Pi Cobbler: Adafruit Pi Cobbler GPIO Breakout for Raspberry Pi
