# Fritzing sketch mcp3008 (saved by Fritzing 0.7.7b)
breadboards: 1

parts:
  Pi1 = Adafruit Pi Cobbler
  R1 = Rotary Potentiometer (Small) [maximum_resistance=100kΩ]
  IC1 = MCP3008 8-channel 10-bit ADC [part_number=MCP3008]

nets:
  N1: Pi1.3V3, R1.leg1, IC1.no_name_yet#15, IC1.no_name_yet#16
  N2: Pi1.GND, R1.leg2, IC1.no_name_yet#9, IC1.no_name_yet#14
  N3: Pi1.MOSI, IC1.no_name_yet#11
  N4: Pi1.MISO, IC1.no_name_yet#12
  N5: Pi1.SCLK, IC1.no_name_yet#13
  N6: Pi1.CE0, IC1.no_name_yet#10
  N7: R1.wiper, IC1.no_name_yet#1

custom parts:
  Adafruit Pi Cobbler: Adafruit Pi Cobbler GPIO Breakout for Raspberry Pi
